# Fritzing sketch Smart_Aquarium (1) (saved by Fritzing 0.9.3b)
breadboards: 1

parts:
  M2 = ph-4502c [package=THT]
  DS1 = DS18B20 1-Wire Temperature Sensor Probe
  J1 = Basic Servo
  R1 = Resistor [tolerance=±5% resistance=1k package=THT]
  R2 = Resistor [tolerance=±5% resistance=2.2k package="1206 [SMD]"]
  M3 = DOIT Esp32 DevKit v1 (30 pins long, 11 pins width) [part_number=ESP32S-PIN30]

nets:
  N1: M2.pin3, R1.Pin_1
  GND: M2.pin4, M2.pin5, DS1.GND, J1.gnd, R2.Pin_1, M3.GND
  VDD: M2.pin6, DS1.VDD, J1.vcc, M3.VIN
  N2: DS1.DQ, M3.D27
  N3: J1.pulse, M3.D12
  N4: R1.Pin_0, R2.Pin_0, M3.D33

custom parts:
  ph-4502c: ph-4502c PH Meter.
  DOIT Esp32 DevKit v1 (30 pins long, 11 pins width): The DOIT Esp32 DevKit v1 is one of the development board created by DOIT to evaluate the ESP-WROOM-32 module. It is based on the ESP32 microcontroller that boasts Wifi, Bluetooth, Ethernet and Low Power support all in a single chip. (vanepp) made breadboard work, adjusted pin numbering and labels and reduced size of schematic and cleaned up pcb. This chip is 30pins long (2 x15) and 11 pins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
